# Fritzing sketch laundrybox (saved by Fritzing 0.9.6)

parts:
  Load_cell = Load cell
  HX711 = HX711
  M5Stack_U107 = M5Stack U107
  Teensy_4_1 = Teensy 4.1
  Raspberry_Pi = Raspberry Pi

nets:
  N1: Load_cell.E+, HX711.E+
  N2: Load_cell.E-, HX711.E-
  N3: Load_cell.A+, HX711.A+
  N4: Load_cell.A-, HX711.A-
  VCC: HX711.VCC, Teensy_4_1.3V3
  N5: HX711.GND, Teensy_4_1.GND#5
  N6: HX711.DT, Teensy_4_1.D2
  N7: HX711.SCK, Teensy_4_1.D3
  5V: M5Stack_U107.5V, Teensy_4_1.5V
  N8: M5Stack_U107.TXD, Teensy_4_1.D0
  N9: M5Stack_U107.RXD, Teensy_4_1.D1
  N10: M5Stack_U107.GND, Teensy_4_1.GND#3
  N11: Teensy_4_1.USB, Raspberry_Pi.USB
